# Fritzing sketch Sensor Design (saved by Fritzing 0.9.3b)
circuit board: 5.48961cm x 2.44691cm
breadboards: 1

parts:
  BME280 = Adafruit BME280
  PMS5003_Breakout = Hirose DF13 Series Header [part_number=DF13#-8P-1.25V package=DF13C-8P-1.25V]
  BME280_2 = Hirose DF13 Series Header [part_number=DF13A-2P-1.25H package=DF13A-2P-1.25H]
  J1 = JST-03JQ-BT [part_number=JST-JQ-BT package=THT]

nets:
  N1: BME280.VIN, J1.pin1
  N2: BME280.GND, PMS5003_Breakout.2, J1.pin2
  N3: BME280.SCK/SCL, BME280_2.2
  N4: BME280.SDI/SDA, BME280_2.1
  N5: PMS5003_Breakout.1, J1.pin3

custom parts:
  Adafruit BME280: Bosch has stepped up their game with their new BME280 sensor, an environmental sensor with temperature, barometric pressure and humidity! This sensor is great for all sorts of weather/environmental sensing and can even be used in both I2C and SPI! This precision sensor from Bosch is the best low-cost sensing solution for measuring humidity with ±3% accuracy, barometric pressure with ±1 hPa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
