# Fritzing sketch Sensor Design (saved by Fritzing 0.9.3b)
circuit board: 11.3034cm x 6.26632cm
breadboards: 2

parts:
  BME280 = Adafruit BME280
  PMS5003 = Hirose DF13 Series Header [part_number=DF13#-8P-1.25V package=DF13C-8P-1.25V]
  J1 = JST-03JQ-BT [part_number=JST-JQ-BT package=THT]
  Status_LED = RGB LED (com. anode, rbg) [package="5 mm [THT]"]  # not connected
  Part1 = Adafruit FeatherWing Proto [part_number="Adafruit #2884"]
  R1 = Resistor [tolerance=±5% resistance=680 package=THT]  # not connected

nets:
  N1: BME280.VIN, J1.pin1, Part1.3V
  GND: BME280.GND, PMS5003.2, J1.pin2, Part1.GND
  N2: PMS5003.1, J1.pin3, Part1.USB

custom parts:
  Adafruit BME280: Bosch has stepped up their game with their new BME280 sensor, an environmental sensor with temperature, barometric pressure and humidity! This sensor is great for all sorts of weather/environmental sensing and can even be used in both I2C and SPI! This precision sensor from Bosch is the best low-cost sensing solution for measuring humidity with ±3% accuracy, barometric pressure with ±1 hPa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
  Adafruit FeatherWing Proto: This is the FeatherWing Proto - a prototyping add-on for all Feather boards. Using our Feather Stacking Headers or Feather Female Headers you can connect a FeatherWing on top or bottom of your Feather board and let the board take flight! This has a duplicate breakout for each pin on a Feather, as well as a bunch of plain grid proto holes. For GND and 3.3V, we give you a strip of connected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
